// Logisim project projeto de circuito 2.circ as structural Verilog: 18 circuits, main circuit main
module main (
  input  Clock,
  input  SelecionaXouY,
  input  SelecionaAouB,
  input  in_4,
  input  in_5,
  input  in_6,
  input  in_7,
  input  in_8,
  input  in_9,
  input  in_10,
  input  in_11,
  input  in_12,
  input  in_13
);

  wire clock_1_out, numerouser_1_out_7, numerouseroeste_1_out_7, Seletor_out_5, Seletor_out_7;
  wire [3:0] \Memoria4bits_saída , numerouser_1_out_6, numerouseroeste_1_out_6, Seletor_out_6, Seletor_out_8;
  wire [4:0] numerouser_1_s, numerouseroeste_1_s;

  LED led_1 (.in(numerouser_1_out_7));
  Hex_Digit_Display hex_digit_display_1 (.value(numerouser_1_out_6));  // open: dp
  NumeroUser numerouser_1 (
    .out_7(numerouser_1_out_7), .out_6(numerouser_1_out_6), .in_1(in_4), .in_2(in_5), .in_3(in_6),
    .in_4(in_7), .in_5(in_8), .S(numerouser_1_s));
  LED led_2 (.in(Seletor_out_5));
  Clock clock_1 (.out(clock_1_out));
  Hex_Digit_Display hex_digit_display_2 (.value(\Memoria4bits_saída ));  // open: dp
  MemoriaNumeroUser Memoria4bits (.Entrada(Seletor_out_6), .Clock(clock_1_out), .\Saída (\Memoria4bits_saída ));
  LED led_3 (.in(Seletor_out_7));
  Hex_Digit_Display hex_digit_display_3 (.value(Seletor_out_8));  // open: dp
  Seletor Seletor (
    .in_1(SelecionaXouY), .in_2(SelecionaAouB), .in_3(numerouser_1_s), .in_4(numerouseroeste_1_s),
    .out_6(Seletor_out_6), .out_8(Seletor_out_8), .out_5(Seletor_out_5), .out_7(Seletor_out_7));
  LED led_4 (.in(numerouseroeste_1_out_7));
  Hex_Digit_Display hex_digit_display_4 (.value(numerouseroeste_1_out_6));  // open: dp
  NumeroUserOeste numerouseroeste_1 (
    .S(numerouseroeste_1_s), .out_7(numerouseroeste_1_out_7), .out_6(numerouseroeste_1_out_6), .in_1(in_9),
    .in_2(in_10), .in_3(in_11), .in_4(in_12), .in_5(in_13));

  // Notes on the sheet:
  //   Jogador A
  //   X
  //   Y
  //   Jogador B
endmodule

module NumeroUser (
  input  in_1,
  input  in_2,
  input  in_3,
  input  in_4,
  input  in_5,
  output [3:0] out_6,
  output out_7,
  output [4:0] S
);


  assign out_6 = {in_2, in_3, in_4, in_5};
  assign out_7 = in_1;
  assign S = {in_1, in_2, in_3, in_4, in_5};
endmodule

// NumeroUser
module NumeroUserOeste (
  input  in_1,
  input  in_2,
  input  in_3,
  input  in_4,
  input  in_5,
  output [3:0] out_6,
  output out_7,
  output [4:0] S
);


  assign out_6 = {in_2, in_3, in_4, in_5};
  assign out_7 = in_1;
  assign S = {in_1, in_2, in_3, in_4, in_5};
endmodule

module Seletor (
  input  in_1,
  input  in_2,
  input  [4:0] in_3,
  input  [4:0] in_4,
  output out_5,
  output [3:0] out_6,
  output out_7,
  output [3:0] out_8
);

  wire [4:0] demultiplexer_1_out0, demultiplexer_1_out1, multiplexer_1_out;

  converte5para4 converte5para4_1 (.out_3(out_5), .in_1(demultiplexer_1_out0), .out_2(out_6));
  Demultiplexer #(.width(5), .enable("false")) demultiplexer_1 (
    .out0(demultiplexer_1_out0), .out1(demultiplexer_1_out1), .in(multiplexer_1_out), .sel(in_1));
  Multiplexer #(.width(5), .enable("false")) multiplexer_1 (
    .in0(in_3), .in1(in_4), .out(multiplexer_1_out), .sel(in_2));
  converte5para4 converte5para4_2 (.out_3(out_7), .in_1(demultiplexer_1_out1), .out_2(out_8));
endmodule

module MemoriaNumeroUser (
  input  Clock,
  input  [3:0] Entrada,
  output [3:0] \Saída 
);

  D_Flip_Flop d_ff_1 (.clk(Clock), .D(Entrada[0]), .Q(\Saída [0]));  // open: Qn, preset, en, reset
  D_Flip_Flop d_ff_2 (.clk(Clock), .D(Entrada[1]), .Q(\Saída [1]));  // open: Qn, preset, en, reset
  D_Flip_Flop d_ff_3 (.clk(Clock), .D(Entrada[2]), .Q(\Saída [2]));  // open: Qn, preset, en, reset
  D_Flip_Flop d_ff_4 (.clk(Clock), .D(Entrada[3]), .Q(\Saída [3]));  // open: Qn, preset, en, reset
endmodule

module RandomNumber (
  input  Clock,
  input  Reset,
  output [4:0] out_3,
  output [4:0] out_4
);

  wire converte5para4_1_out_3, converte5para4_2_out_3;
  wire [3:0] converte5para4_1_out_2, converte5para4_2_out_2;

  LED led_1 (.in(converte5para4_2_out_3));
  LED led_2 (.in(converte5para4_1_out_3));
  Hex_Digit_Display hex_digit_display_1 (.value(converte5para4_1_out_2));  // open: dp
  converte5para4 converte5para4_1 (.out_3(converte5para4_1_out_3), .in_1(out_3), .out_2(converte5para4_1_out_2));
  Random #(.width(5)) random_1 (.clk(Clock), .out(out_3), .clr(Reset));  // open: next
  Random #(.width(5)) random_2 (.clk(Clock), .out(out_4), .clr(Reset));  // open: next
  converte5para4 converte5para4_2 (.out_3(converte5para4_2_out_3), .in_1(out_4), .out_2(converte5para4_2_out_2));
  Hex_Digit_Display hex_digit_display_2 (.value(converte5para4_2_out_2));  // open: dp
  D_Flip_Flop d_ff_1 ();  // open: clk, D, Q, Qn, preset, en, reset
endmodule

module converte5para4 (
  input  [4:0] in_1,
  output [3:0] out_2,
  output out_3
);


  assign out_2 = in_1[3:0];
  assign out_3 = in_1[4];
endmodule

module Comparador (
  input  [4:0] X_random,
  input  [4:0] Y_random,
  input  [4:0] X_user,
  input  [4:0] Y_user
);

  wire [5:0] somador_2_out_3, Somador_out_3;

  Somador Somador (.X(X_random), .Y(Y_random), .out_3(Somador_out_3));
  Somador somador_2 (.X(X_user), .Y(Y_user), .out_3(somador_2_out_3));
endmodule

module Somador (
  input  [4:0] X,
  input  [4:0] Y,
  output [5:0] out_3
);

  wire [1:0] Converte5_para_4_1_out_3;
  wire [3:0] adder_1_out, adder_2_out, adder_3_out, adder_4_out, Converte5_para_4_1_2_out_2,
       Converte5_para_4_1_out_2, multiplexer_1_out, multiplexer_2_out, negator_1_out, negator_2_out,
       negator_3_out, negator_4_out;
  wire [4:4] adder_1_cout, adder_4_cout;
  wire [5:5] comparator_1_lt, not_1_out;

  converte5para4 Converte5_para_4_1 (.out_3(Converte5_para_4_1_out_3[0]), .in_1(X), .out_2(Converte5_para_4_1_out_2));
  converte5para4 Converte5_para_4_1_2 (
    .out_3(Converte5_para_4_1_out_3[1]), .in_1(Y), .out_2(Converte5_para_4_1_2_out_2));
  Negator #(.width(4)) negator_1 (.in(Converte5_para_4_1_out_2), .out(negator_1_out));
  Negator #(.width(4)) negator_2 (.in(Converte5_para_4_1_2_out_2), .out(negator_2_out));
  Adder #(.width(4)) adder_1 (
    .a(Converte5_para_4_1_out_2), .b(Converte5_para_4_1_2_out_2), .out(adder_1_out), .cout(adder_1_cout[4]));  // open: cin
  Adder #(.width(4)) adder_2 (.a(negator_1_out), .b(Converte5_para_4_1_2_out_2), .out(adder_2_out));  // open: cin, cout
  Comparator #(.width(4)) comparator_1 (
    .a(Converte5_para_4_1_out_2), .b(Converte5_para_4_1_2_out_2), .lt(comparator_1_lt[5]));  // open: gt, eq
  not not_1 (not_1_out[5], comparator_1_lt[5]);
  Adder #(.width(4)) adder_3 (.a(Converte5_para_4_1_out_2), .b(negator_2_out), .out(adder_3_out));  // open: cin, cout
  Adder #(.width(4)) adder_4 (
    .a(Converte5_para_4_1_out_2), .b(Converte5_para_4_1_2_out_2), .out(adder_4_out), .cout(adder_4_cout[4]));  // open: cin
  Multiplexer #(.width(4), .enable("false")) multiplexer_1 (
    .in0(adder_2_out), .in1(negator_3_out), .out(multiplexer_1_out), .sel(comparator_1_lt[5]));
  Negator #(.width(4)) negator_3 (.in(adder_2_out), .out(negator_3_out));
  Multiplexer #(.width(4), .enable("false")) multiplexer_2 (
    .in0(adder_3_out), .in1(negator_4_out), .out(multiplexer_2_out), .sel(not_1_out[5]));
  Negator #(.width(4)) negator_4 (.in(adder_3_out), .out(negator_4_out));
  Multiplexer #(.select(2), .width(6), .enable("false")) multiplexer_3 (
    .in0({1'b0, adder_1_cout[4], adder_1_out}), .in1({comparator_1_lt[5], 1'b0, multiplexer_1_out}),
    .in2({not_1_out[5], 1'b0, multiplexer_2_out}), .in3({1'b1, adder_4_cout[4], adder_4_out}), .out(out_3),
    .sel(Converte5_para_4_1_out_3));
endmodule

module Flip_Flop_D_subida (
  input  D,
  output Q,
  output nQ
);

  wire CLK_out, nand_1_out, nand_2_out;

  Clock CLK (.out(CLK_out));
  nand nand_1 (nand_1_out, D, CLK_out);
  nand nand_2 (nand_2_out, CLK_out, ~D);  // NAND_Gate
  nand nand_3 (Q, nand_1_out, nQ);
  nand nand_4 (nQ, Q, nand_2_out);

  // Notes on the sheet:
  //   O flip flop tipo D serve para guardar um valor.
endmodule

module \Circuito_de_9_à_0  (
  input  Q3,
  input  Q2,
  input  Q1,
  input  Q0,
  output S3,
  output S2,
  output S1,
  output S0
);

  wire and_1_out, and_2_out, and_3_out, and_4_out, and_5_out, and_6_out, and_7_out, and_8_out, and_9_out,
       not_1_out, not_2_out, not_3_out, not_4_out, not_5_out, not_6_out, not_7_out, not_8_out, not_9_out,
       not_10_out;

  not not_1 (not_1_out, Q3);
  not not_2 (not_2_out, Q2);
  not not_3 (not_3_out, Q1);
  not not_4 (not_4_out, Q0);
  not not_5 (not_5_out, Q1);
  not not_6 (not_6_out, Q0);
  not not_7 (not_7_out, Q1);
  not not_8 (not_8_out, Q0);
  not not_9 (not_9_out, Q1);
  not not_10 (not_10_out, Q0);
  not not_11 (S0, Q0);
  and and_1 (and_1_out, not_1_out, not_2_out, not_3_out, not_4_out);
  and and_2 (and_2_out, Q3, Q0);
  and and_3 (and_3_out, Q3, Q1);
  and and_4 (and_4_out, Q2, Q0);
  and and_5 (and_5_out, Q2, Q1);
  and and_6 (and_6_out, Q3, not_5_out, not_6_out);
  and and_7 (and_7_out, Q1, Q0);
  and and_8 (and_8_out, Q2, not_7_out, not_8_out);
  and and_9 (and_9_out, Q3, not_9_out, not_10_out);
  or or_1 (S3, and_1_out, and_2_out, and_3_out);
  or or_2 (S2, and_4_out, and_5_out, and_6_out);
  or or_3 (S1, and_7_out, and_8_out, and_9_out);

  // Notes on the sheet:
  //   Circuito para usar no contador de 0 à 9
endmodule

module \Contador_de_9_à_0_unidade_seg_e_min  (
  input  CLOCK,
  input  tempo,
  input  MOD,
  input  ENABLE,
  input  CLEAR,
  output saida_de_0,
  output [3:0] out_7,
  output out_8,
  output out_9,
  output out_10,
  output out_11
);

  wire d_ff_1_q, d_ff_2_q, d_ff_3_q, d_ff_4_q, multiplexer_1_out, not_1_out;

  Multiplexer multiplexer_1 (.in0(CLOCK), .in1(tempo), .out(multiplexer_1_out), .sel(not_1_out));  // open: en
  not not_1 (not_1_out, MOD);
  D_Flip_Flop d_ff_1 (
    .clk(multiplexer_1_out), .D(out_7[3]), .Q(d_ff_1_q), .Qn(out_11), .en(ENABLE), .reset(CLEAR));  // open: preset
  D_Flip_Flop d_ff_2 (
    .clk(multiplexer_1_out), .D(out_7[2]), .Q(d_ff_2_q), .Qn(out_10), .en(ENABLE));  // open: preset, reset
  D_Flip_Flop d_ff_3 (
    .clk(multiplexer_1_out), .D(out_7[1]), .Q(d_ff_3_q), .Qn(out_9), .en(ENABLE));  // open: preset, reset
  QUANDO_FOR_0_de_9 quando_for_0_de_9_1 (
    .Q3(d_ff_1_q), .Q2(d_ff_2_q), .Q1(d_ff_3_q), .Q0(d_ff_4_q), .S4(saida_de_0), .S3(out_7[3]),
    .S2(out_7[2]), .S1(out_7[1]), .S0(out_7[0]));
  D_Flip_Flop d_ff_4 (
    .clk(multiplexer_1_out), .D(out_7[0]), .Q(d_ff_4_q), .Qn(out_8), .en(ENABLE), .reset(CLEAR));  // open: preset
  Hex_Digit_Display hex_digit_display_1 (.value(out_7));  // open: dp

  // Notes on the sheet:
  //   3
  //   unidades de segundos e minutos
  //   2
  //   QUnado apertar o start ele comeca a contar
  //   Quando o mode tá em 1 o relógio funciona com o clock normal, se vai ta normal ou no config
  //   E quando o start vai pra 1, ele fica parado e não responde nem ao clock nem ao botão de alterar
  //   1
  //   Quando vai pra 0, o relógio para de mudar com o clock e você pode apertar o "tempo" pra editar, função de chaveamento 
  //   0
endmodule

module \Contador_de_5_à_0_dezena_dos_minutos  (
  input  CLK,
  input  CLK_2,
  input  CLK_3,
  input  CLOCK,
  input  tempo,
  input  MOD,
  input  Clear,
  input  enable,
  output Sinal_de_0,
  output [3:0] out_10,
  output SAIDA_3,
  output SAIDA_2,
  output SAIDA_1
);

  wire and_1_out, d_ff_1_q, d_ff_2_q, d_ff_3_q, multiplexer_1_out, not_1_out;

  and and_1 (and_1_out, CLK, CLK_2, CLK_3, CLOCK);
  not not_1 (not_1_out, MOD);
  Multiplexer multiplexer_1 (.in0(and_1_out), .in1(tempo), .out(multiplexer_1_out), .sel(not_1_out));  // open: en
  D_Flip_Flop d_ff_1 (
    .clk(multiplexer_1_out), .D(out_10[0]), .Q(d_ff_1_q), .Qn(SAIDA_1), .en(enable), .reset(Clear));  // open: preset
  D_Flip_Flop d_ff_2 (
    .clk(multiplexer_1_out), .D(out_10[1]), .Q(d_ff_2_q), .Qn(SAIDA_2), .en(enable), .reset(Clear));  // open: preset
  D_Flip_Flop d_ff_3 (
    .clk(multiplexer_1_out), .D(out_10[2]), .Q(d_ff_3_q), .Qn(SAIDA_3), .en(enable), .reset(Clear));  // open: preset
  quando_for_0_de_5 quando_for_0_de_5_1 (
    .Q2(d_ff_3_q), .Q1(d_ff_2_q), .Q0(d_ff_1_q), .S3(Sinal_de_0), .S2(out_10[2]), .S1(out_10[1]),
    .S0(out_10[0]));
  Hex_Digit_Display hex_digit_display_1 (.value({1'b0, out_10[2:0]}));  // open: dp

  assign out_10[3] = 1'b0;

  // Notes on the sheet:
  //   dezena dos minutos
  //   vez do jogador 
  //   se o jogo esta rodando
  //   se a entrada anterior ficou menor que 0
endmodule

module \Circuito_de_5_à_0  (
  input  Q3,
  input  Q2,
  input  Q1,
  output S3,
  output S2,
  output S1
);

  wire and_1_out, and_2_out, and_3_out, and_4_out, not_1_out, not_2_out, not_3_out, not_4_out;

  not not_1 (not_1_out, Q3);
  not not_2 (not_2_out, Q2);
  not not_3 (not_3_out, Q1);
  not not_4 (not_4_out, Q1);
  not not_5 (S1, Q1);
  and and_1 (and_1_out, not_1_out, not_2_out, not_3_out);
  and and_2 (and_2_out, Q3, Q1);
  and and_3 (and_3_out, Q2, Q1);
  and and_4 (and_4_out, Q3, not_4_out);
  or or_1 (S3, and_1_out, and_2_out);
  or or_2 (S2, and_3_out, and_4_out);
endmodule

module \Copia_do_0_à_9_unidade_de_minutos  (
  input  CLK,
  input  CLK_2,
  input  CLOCK,
  input  tempo,
  input  MOD,
  input  CLEAR,
  input  ENABLE,
  output saida_de_0,
  output [3:0] out_9,
  output SAIDA_3,
  output SAIDA_2,
  output SAIDA_1,
  output SAIDA_0
);

  wire and_1_out, d_ff_1_q, d_ff_2_q, d_ff_3_q, d_ff_4_q, multiplexer_1_out, not_1_out;

  and and_1 (and_1_out, CLK, CLK_2, CLOCK);
  not not_1 (not_1_out, MOD);
  Multiplexer multiplexer_1 (.in0(and_1_out), .in1(tempo), .out(multiplexer_1_out), .sel(not_1_out));  // open: en
  D_Flip_Flop d_ff_1 (
    .clk(multiplexer_1_out), .D(out_9[3]), .Q(d_ff_1_q), .Qn(SAIDA_0), .en(ENABLE), .reset(CLEAR));  // open: preset
  D_Flip_Flop d_ff_2 (
    .clk(multiplexer_1_out), .D(out_9[2]), .Q(d_ff_2_q), .Qn(SAIDA_1), .en(ENABLE), .reset(CLEAR));  // open: preset
  D_Flip_Flop d_ff_3 (
    .clk(multiplexer_1_out), .D(out_9[1]), .Q(d_ff_3_q), .Qn(SAIDA_2), .en(ENABLE), .reset(CLEAR));  // open: preset
  QUANDO_FOR_0_de_9 quando_for_0_de_9_1 (
    .Q3(d_ff_1_q), .Q2(d_ff_2_q), .Q1(d_ff_3_q), .Q0(d_ff_4_q), .S4(saida_de_0), .S3(out_9[3]),
    .S2(out_9[2]), .S1(out_9[1]), .S0(out_9[0]));
  D_Flip_Flop d_ff_4 (
    .clk(multiplexer_1_out), .D(out_9[0]), .Q(d_ff_4_q), .Qn(SAIDA_3), .en(ENABLE), .reset(CLEAR));  // open: preset
  Hex_Digit_Display hex_digit_display_1 (.value(out_9));  // open: dp

  // Notes on the sheet:
  //   unidades de  minutos
endmodule

module cronometro (
  input  reset,
  input  \time ,
  input  time_2,
  input  time_3,
  input  time_4,
  input  mod,
  input  in_7
);

  wire and_1_out, and_2_out, clock_1_out, \contador_de_5_à_0_dezena_dos_minutos_1_saida_1 ,
       \contador_de_5_à_0_dezena_dos_minutos_1_saida_2 , \contador_de_5_à_0_dezena_dos_minutos_1_saida_3 ,
       \contador_de_5_à_0_dezena_dos_minutos_1_sinal_de_0 ,
       \contador_de_5_à_0_dezena_dos_minutos_2_sinal_de_0 , \contador_de_9_à_0_unidade_seg_e_min_1_out_8 ,
       \contador_de_9_à_0_unidade_seg_e_min_1_out_9 , \contador_de_9_à_0_unidade_seg_e_min_1_out_10 ,
       \contador_de_9_à_0_unidade_seg_e_min_1_out_11 , \contador_de_9_à_0_unidade_seg_e_min_1_saida_de_0 ,
       \copia_do_0_à_9_unidade_de_minutos_1_saida_0 , \copia_do_0_à_9_unidade_de_minutos_1_saida_1 ,
       \copia_do_0_à_9_unidade_de_minutos_1_saida_2 , \copia_do_0_à_9_unidade_de_minutos_1_saida_3 ,
       \copia_do_0_à_9_unidade_de_minutos_1_saida_de_0 ;
  wire [3:0] \contador_de_5_à_0_dezena_dos_minutos_1_out_10 ,
       \contador_de_5_à_0_dezena_dos_minutos_2_out_10 , \contador_de_9_à_0_unidade_seg_e_min_1_out_7 ,
       \copia_do_0_à_9_unidade_de_minutos_1_out_9 ;

  Clock clock_1 (.out(clock_1_out));
  and and_1 (and_1_out, in_7, ~and_2_out);  // AND_Gate
  \Contador_de_9_à_0_unidade_seg_e_min  \contador_de_9_à_0_unidade_seg_e_min_1  (
    .CLOCK(clock_1_out), .tempo(\time ), .MOD(mod), .out_7(\contador_de_9_à_0_unidade_seg_e_min_1_out_7 ),
    .ENABLE(and_1_out), .CLEAR(reset), .out_8(\contador_de_9_à_0_unidade_seg_e_min_1_out_8 ),
    .out_9(\contador_de_9_à_0_unidade_seg_e_min_1_out_9 ),
    .out_10(\contador_de_9_à_0_unidade_seg_e_min_1_out_10 ),
    .out_11(\contador_de_9_à_0_unidade_seg_e_min_1_out_11 ),
    .saida_de_0(\contador_de_9_à_0_unidade_seg_e_min_1_saida_de_0 ));
  \Contador_de_5_à_0_dezena_dos_minutos  \contador_de_5_à_0_dezena_dos_minutos_1  (
    .out_10(\contador_de_5_à_0_dezena_dos_minutos_1_out_10 ),
    .SAIDA_3(\contador_de_5_à_0_dezena_dos_minutos_1_saida_3 ),
    .SAIDA_2(\contador_de_5_à_0_dezena_dos_minutos_1_saida_2 ),
    .SAIDA_1(\contador_de_5_à_0_dezena_dos_minutos_1_saida_1 ), .Clear(reset),
    .CLOCK(\contador_de_9_à_0_unidade_seg_e_min_1_out_10 ), .tempo(time_2), .MOD(mod),
    .CLK_3(\contador_de_9_à_0_unidade_seg_e_min_1_out_9 ),
    .CLK_2(\contador_de_9_à_0_unidade_seg_e_min_1_out_8 ),
    .CLK(\contador_de_9_à_0_unidade_seg_e_min_1_out_11 ),
    .Sinal_de_0(\contador_de_5_à_0_dezena_dos_minutos_1_sinal_de_0 ), .enable(and_1_out));
  \Copia_do_0_à_9_unidade_de_minutos  \copia_do_0_à_9_unidade_de_minutos_1  (
    .CLK(\contador_de_5_à_0_dezena_dos_minutos_1_saida_3 ),
    .CLK_2(\contador_de_5_à_0_dezena_dos_minutos_1_saida_2 ),
    .CLOCK(\contador_de_5_à_0_dezena_dos_minutos_1_saida_1 ), .tempo(time_3), .MOD(mod), .ENABLE(and_1_out),
    .CLEAR(reset), .saida_de_0(\copia_do_0_à_9_unidade_de_minutos_1_saida_de_0 ),
    .out_9(\copia_do_0_à_9_unidade_de_minutos_1_out_9 ),
    .SAIDA_3(\copia_do_0_à_9_unidade_de_minutos_1_saida_3 ),
    .SAIDA_2(\copia_do_0_à_9_unidade_de_minutos_1_saida_2 ),
    .SAIDA_1(\copia_do_0_à_9_unidade_de_minutos_1_saida_1 ),
    .SAIDA_0(\copia_do_0_à_9_unidade_de_minutos_1_saida_0 ));
  Hex_Digit_Display hex_digit_display_1 (.value(\contador_de_5_à_0_dezena_dos_minutos_2_out_10 ));  // open: dp
  \Contador_de_5_à_0_dezena_dos_minutos  \contador_de_5_à_0_dezena_dos_minutos_2  (
    .out_10(\contador_de_5_à_0_dezena_dos_minutos_2_out_10 ), .Clear(reset),
    .CLOCK(\copia_do_0_à_9_unidade_de_minutos_1_saida_1 ), .tempo(time_4), .MOD(mod),
    .CLK_3(\copia_do_0_à_9_unidade_de_minutos_1_saida_2 ),
    .CLK_2(\copia_do_0_à_9_unidade_de_minutos_1_saida_3 ),
    .CLK(\copia_do_0_à_9_unidade_de_minutos_1_saida_0 ),
    .Sinal_de_0(\contador_de_5_à_0_dezena_dos_minutos_2_sinal_de_0 ), .enable(and_1_out));  // open: SAIDA_3, SAIDA_2, SAIDA_1
  Hex_Digit_Display hex_digit_display_2 (.value(\copia_do_0_à_9_unidade_de_minutos_1_out_9 ));  // open: dp
  and and_2 (and_2_out, \contador_de_5_à_0_dezena_dos_minutos_2_sinal_de_0 , \copia_do_0_à_9_unidade_de_minutos_1_saida_de_0 , \contador_de_5_à_0_dezena_dos_minutos_1_sinal_de_0 , \contador_de_9_à_0_unidade_seg_e_min_1_saida_de_0 );
  Hex_Digit_Display hex_digit_display_3 (.value(\contador_de_5_à_0_dezena_dos_minutos_1_out_10 ));  // open: dp
  Hex_Digit_Display hex_digit_display_4 (.value(\contador_de_9_à_0_unidade_seg_e_min_1_out_7 ));  // open: dp
endmodule

module QUANDO_FOR_0_de_9 (
  input  Q3,
  input  Q2,
  input  Q1,
  input  Q0,
  output S4,
  output S3,
  output S2,
  output S1,
  output S0
);

  wire and_1_out, and_2_out, and_3_out, and_4_out, and_5_out, and_6_out, and_8_out, and_9_out, not_1_out,
       not_2_out, not_3_out, not_4_out, not_5_out, not_6_out, not_7_out, not_8_out, not_9_out, not_10_out,
       not_11_out;

  not not_1 (not_1_out, Q3);
  not not_2 (not_2_out, Q2);
  not not_3 (not_3_out, Q1);
  not not_4 (not_4_out, Q3);
  not not_5 (not_5_out, Q2);
  not not_6 (not_6_out, Q1);
  not not_7 (not_7_out, Q0);
  and and_1 (and_1_out, Q2, Q0);
  and and_2 (and_2_out, Q2, Q1);
  and and_3 (and_3_out, Q3, not_8_out);
  not not_8 (not_8_out, Q0);
  and and_4 (and_4_out, Q1, Q0);
  and and_5 (and_5_out, Q2, not_9_out, not_10_out);
  not not_9 (not_9_out, Q1);
  not not_10 (not_10_out, Q0);
  and and_6 (and_6_out, Q3, not_11_out);
  not not_11 (not_11_out, Q0);
  not not_12 (S0, Q0);
  and and_7 (S4, not_1_out, not_2_out, not_3_out, Q0);
  and and_8 (and_8_out, not_4_out, not_5_out, not_6_out, not_7_out);
  or or_1 (S3, and_8_out, and_9_out);
  and and_9 (and_9_out, Q3, Q0);
  or or_2 (S2, and_1_out, and_2_out, and_3_out);
  or or_3 (S1, and_4_out, and_5_out, and_6_out);
endmodule

module quando_for_0_de_5 (
  input  Q2,
  input  Q1,
  input  Q0,
  output S3,
  output S2,
  output S1,
  output S0
);

  wire and_2_out, and_3_out, and_4_out, and_5_out, not_1_out, not_2_out, not_3_out, not_4_out, not_5_out,
       not_6_out;

  not not_1 (not_1_out, Q2);
  not not_2 (not_2_out, Q1);
  not not_3 (not_3_out, Q2);
  not not_4 (not_4_out, Q1);
  not not_5 (not_5_out, Q0);
  not not_6 (not_6_out, Q0);
  not not_7 (S0, Q0);
  and and_1 (S3, not_1_out, not_2_out, Q0);
  and and_2 (and_2_out, not_3_out, not_4_out, not_5_out);
  and and_3 (and_3_out, Q2, Q0);
  and and_4 (and_4_out, Q1, Q0);
  and and_5 (and_5_out, Q2, not_6_out);
  or or_1 (S2, and_2_out, and_3_out);
  or or_2 (S1, and_4_out, and_5_out);
endmodule
